# Fritzing sketch Numato_Wiring (saved by Fritzing 0.9.4)
breadboards: 1

parts:
  S1 = Pushbutton [package="[THT]"]
  R1 = Resistor [tolerance=±5% resistance=220 package="2010 [SMD]"]

nets:
  N1: S1.Pin_1, S1.Pin_2
  N2: S1.Pin_3, S1.Pin_4, R1.Pin_1

notes:
  Numato USB Powered Relay
  Ground
  IO3
  IO2
  IO1
  IO0
